// Logisim project 桶形移位器.circ as structural Verilog: 1 circuit, main circuit main
module main (
  input  _0,
  input  A_L,
  input  I7,
  input  I6,
  input  I5,
  input  I4,
  input  I3,
  input  I2,
  input  I1,
  input  I0,
  input  _0_2,
  input  b0,
  input  b1,
  input  b2,
  input  L_R,
  output out_16,
  output out_17,
  output out_18,
  output out_19,
  output out_20,
  output out_21,
  output out_22,
  output out_23
);

  wire multiplexer_2_out, multiplexer_3_out, multiplexer_4_out, multiplexer_5_out, multiplexer_6_out,
       multiplexer_7_out, multiplexer_8_out, multiplexer_9_out, multiplexer_10_out, multiplexer_11_out,
       multiplexer_12_out, multiplexer_13_out, multiplexer_14_out, multiplexer_15_out, multiplexer_16_out,
       multiplexer_17_out;

  Multiplexer #(.disabled(0), .enable("false")) multiplexer_1 (.in0(I7), .in1(_0), .out(I7), .sel(A_L));
  Multiplexer #(.select(2), .disabled(0)) multiplexer_2 (
    .in0(I7), .in1(I7), .in2(I7), .in3(I6), .out(multiplexer_2_out), .en(b0));  // open: sel
  Multiplexer #(.select(2), .disabled(0)) multiplexer_3 (
    .in0(I6), .in1(I7), .in2(I6), .in3(I5), .out(multiplexer_3_out), .en(b0));  // open: sel
  Multiplexer #(.select(2), .disabled(0)) multiplexer_4 (
    .in0(I5), .in1(I6), .in2(I5), .in3(I4), .out(multiplexer_4_out), .en(b0));  // open: sel
  Multiplexer #(.select(2), .disabled(0)) multiplexer_5 (
    .in0(I4), .in1(I5), .in2(I4), .in3(I3), .out(multiplexer_5_out), .en(b0));  // open: sel
  Multiplexer #(.select(2), .disabled(0)) multiplexer_6 (
    .in0(I3), .in1(I4), .in2(I3), .in3(I2), .out(multiplexer_6_out), .en(b0));  // open: sel
  Multiplexer #(.select(2), .disabled(0)) multiplexer_7 (
    .in0(I2), .in1(I3), .in2(I2), .in3(I1), .out(multiplexer_7_out), .en(b0));  // open: sel
  Multiplexer #(.select(2), .disabled(0)) multiplexer_8 (
    .in0(I1), .in1(I2), .in2(I1), .in3(I0), .out(multiplexer_8_out), .en(b0));  // open: sel
  Multiplexer #(.select(2), .disabled(0)) multiplexer_9 (
    .in0(I0), .in1(I1), .in2(I0), .in3(_0_2), .out(multiplexer_9_out), .en(_0_2));  // open: sel
  Multiplexer #(.select(2), .disabled(0)) multiplexer_10 (
    .in0(multiplexer_2_out), .in1(I7), .in2(multiplexer_2_out), .in3(multiplexer_4_out),
    .out(multiplexer_10_out), .en(b1));  // open: sel
  Multiplexer #(.select(2), .disabled(0)) multiplexer_11 (
    .in0(multiplexer_3_out), .in1(I7), .in2(multiplexer_3_out), .in3(multiplexer_5_out),
    .out(multiplexer_11_out), .en(b1));  // open: sel
  Multiplexer #(.select(2), .disabled(0)) multiplexer_12 (
    .in0(multiplexer_4_out), .in1(multiplexer_2_out), .in2(multiplexer_4_out), .in3(multiplexer_6_out),
    .out(multiplexer_12_out), .en(b1));  // open: sel
  Multiplexer #(.select(2), .disabled(0)) multiplexer_13 (
    .in0(multiplexer_5_out), .in1(I7), .in2(multiplexer_5_out), .in3(multiplexer_7_out),
    .out(multiplexer_13_out), .en(b1));  // open: sel
  Multiplexer #(.select(2), .disabled(0)) multiplexer_14 (
    .in0(multiplexer_6_out), .in1(multiplexer_4_out), .in2(multiplexer_6_out), .in3(multiplexer_8_out),
    .out(multiplexer_14_out), .en(b1));  // open: sel
  Multiplexer #(.select(2), .disabled(0)) multiplexer_15 (
    .in0(multiplexer_7_out), .in1(multiplexer_5_out), .in2(multiplexer_7_out), .in3(multiplexer_9_out),
    .out(multiplexer_15_out), .en(b1));  // open: sel
  Multiplexer #(.select(2), .disabled(0)) multiplexer_16 (
    .in0(multiplexer_8_out), .in1(multiplexer_6_out), .in2(multiplexer_8_out), .in3(_0_2),
    .out(multiplexer_16_out), .en(b1));  // open: sel
  Multiplexer #(.select(2), .disabled(0)) multiplexer_17 (
    .in0(multiplexer_9_out), .in1(multiplexer_7_out), .in2(multiplexer_9_out), .in3(_0_2),
    .out(multiplexer_17_out), .en(_0_2));  // open: sel
  Multiplexer #(.select(2), .disabled(0)) multiplexer_18 (
    .in0(multiplexer_10_out), .in1(I7), .in2(multiplexer_10_out), .in3(multiplexer_14_out), .out(out_16),
    .en(b2));  // open: sel
  Multiplexer #(.select(2), .disabled(0)) multiplexer_19 (
    .in0(multiplexer_11_out), .in1(I7), .in2(multiplexer_11_out), .in3(multiplexer_15_out), .out(out_17),
    .en(b2));  // open: sel
  Multiplexer #(.select(2), .disabled(0)) multiplexer_20 (
    .in0(multiplexer_12_out), .in1(I7), .in2(multiplexer_12_out), .in3(multiplexer_16_out), .out(out_18),
    .en(b2));  // open: sel
  Multiplexer #(.select(2), .disabled(0)) multiplexer_21 (
    .in0(multiplexer_13_out), .in1(I7), .in2(multiplexer_13_out), .in3(multiplexer_17_out), .out(out_19),
    .en(b2));  // open: sel
  Multiplexer #(.select(2), .disabled(0)) multiplexer_22 (
    .in0(multiplexer_14_out), .in1(multiplexer_10_out), .in2(multiplexer_14_out), .in3(_0_2), .out(out_20),
    .en(b2));  // open: sel
  Multiplexer #(.select(2), .disabled(0)) multiplexer_23 (
    .in0(multiplexer_15_out), .in1(multiplexer_11_out), .in2(multiplexer_15_out), .in3(_0_2), .out(out_21),
    .en(b2));  // open: sel
  Multiplexer #(.select(2), .disabled(0)) multiplexer_24 (
    .in0(multiplexer_16_out), .in1(multiplexer_12_out), .in2(multiplexer_16_out), .in3(_0_2), .out(out_22),
    .en(b2));  // open: sel
  Multiplexer #(.select(2), .disabled(0)) multiplexer_25 (
    .in0(multiplexer_17_out), .in1(multiplexer_13_out), .in2(multiplexer_17_out), .in3(_0_2), .out(out_23),
    .en(b2));  // open: sel
endmodule
