// Logisim project 比较器 定序型.circ as structural Verilog: 1 circuit, main circuit main
module main (
  input  en,
  input  RST,
  input  [7:0] in_3,
  output out_4
);

  wire A_2_q, A_2_qn, and_1_out, and_2_out, and_3_out, and_4_out, and_5_out, B_q, B_qn, clock_1_out,
       d_ff_1_q, d_ff_1_qn, D_q, D_qn, not_1_out, not_2_out, or_1_out, or_2_out, or_3_out;
  wire [7:0] A_q, controlled_buffer_1_out, controlled_buffer_2_out, register_1_q;

  Clock clock_1 (.out(clock_1_out));
  and and_1 (and_1_out, not_1_out, B_q);
  not not_1 (not_1_out, clock_1_out);
  and and_2 (and_2_out, D_qn, d_ff_1_qn, B_qn, A_2_qn);
  or or_1 (or_1_out, A_2_q, and_3_out);
  and and_3 (and_3_out, not_2_out, D_q);
  or or_2 (or_2_out, B_q, and_4_out);
  and and_4 (and_4_out, out_4, D_q);
  Register A (.D(register_1_q), .Q(A_q), .clk(and_1_out), .clr(RST));  // open: en
  Register register_1 (.D(in_3), .Q(register_1_q), .clk(and_5_out), .clr(RST));  // open: en
  and and_5 (and_5_out, not_1_out, or_3_out);
  D_Flip_Flop A_2 (.clk(clock_1_out), .D(and_2_out), .Q(A_2_q), .Qn(A_2_qn), .en(en), .reset(RST));  // open: preset
  D_Flip_Flop B (.clk(clock_1_out), .D(or_1_out), .Q(B_q), .Qn(B_qn), .en(en), .reset(RST));  // open: preset
  D_Flip_Flop d_ff_1 (
    .clk(clock_1_out), .D(or_2_out), .Q(d_ff_1_q), .Qn(d_ff_1_qn), .en(en), .reset(RST));  // open: preset
  D_Flip_Flop D (.clk(clock_1_out), .D(d_ff_1_q), .Q(D_q), .Qn(D_qn), .en(en), .reset(RST));  // open: preset
  or or_3 (or_3_out, A_2_q, d_ff_1_q);
  assign controlled_buffer_1_out = D_q ? A_q : 8'bz;  // Controlled_Buffer controlled_buffer_1
  assign controlled_buffer_2_out = D_q ? register_1_q : 8'bz;  // Controlled_Buffer controlled_buffer_2
  not not_2 (not_2_out, out_4);
  Comparator comparator_1 (.a(controlled_buffer_1_out), .b(controlled_buffer_2_out), .gt(out_4));  // open: eq, lt

  // Notes on the sheet:
  //   T
  //   LDRA
  //   B
  //   C
  //   LDRB
  //   CAP
  //   A>B
endmodule
