// Logisim project 比较器 计数器.circ as structural Verilog: 1 circuit, main circuit main
module main (
  input  RST,
  input  [7:0] in_2,
  input  en,
  output out_4
);

  wire and_1_out, and_2_out, and_3_out, B_q, B_qn, clock_1_out, d_ff_1_q, d_ff_1_qn, or_1_out, or_2_out,
       xnor_1_out;
  wire [7:0] A_q, controlled_buffer_1_out, controlled_buffer_2_out, register_1_q;

  Clock clock_1 (.out(clock_1_out));
  and and_1 (and_1_out, d_ff_1_q, B_qn);
  or or_1 (or_1_out, d_ff_1_q, and_2_out);
  xnor xnor_1 (xnor_1_out, d_ff_1_q, B_q);
  D_Flip_Flop d_ff_1 (
    .clk(clock_1_out), .D(or_2_out), .Q(d_ff_1_q), .Qn(d_ff_1_qn), .en(en), .reset(RST));  // open: preset
  D_Flip_Flop B (.clk(clock_1_out), .D(or_1_out), .Q(B_q), .Qn(B_qn), .en(en), .reset(RST));  // open: preset
  or or_2 (or_2_out, B_qn, d_ff_1_qn);
  and and_2 (and_2_out, B_q, out_4);
  Register A (.D(register_1_q), .Q(A_q), .clk(and_1_out), .clr(RST));  // open: en
  Register register_1 (.D(in_2), .Q(register_1_q), .clk(xnor_1_out), .clr(RST));  // open: en
  assign controlled_buffer_1_out = and_3_out ? A_q : 8'bz;  // Controlled_Buffer controlled_buffer_1
  assign controlled_buffer_2_out = and_3_out ? register_1_q : 8'bz;  // Controlled_Buffer controlled_buffer_2
  and and_3 (and_3_out, B_q, d_ff_1_qn);
  Comparator comparator_1 (.a(controlled_buffer_1_out), .b(controlled_buffer_2_out), .gt(out_4));  // open: eq, lt

  // Notes on the sheet:
  //   T
  //   LDRA
  //   B
  //   LDRB
  //   A
  //   CAP
  //   A>B
endmodule
