// Logisim project 比较器 选择器.circ as structural Verilog: 1 circuit, main circuit main
module main (
  input  en,
  input  RST,
  input  [7:0] in_3,
  output out_4
);

  wire and_1_out, and_2_out, clock_1_out, d_ff_1_qn, d_ff_2_qn, multiplexer_1_out, multiplexer_2_out,
       xnor_1_out;
  wire [1:0] d_ff_1_q;
  wire [7:0] A_q, controlled_buffer_1_out, controlled_buffer_2_out, register_1_q;

  Clock clock_1 (.out(clock_1_out));
  and and_1 (and_1_out, d_ff_1_q[0], d_ff_2_qn);
  Multiplexer #(.select(2)) multiplexer_1 (
    .in0(1'b1), .in1(1'b1), .in2(1'b1), .in3(1'b0), .out(multiplexer_1_out), .sel(d_ff_1_q), .en(en));
  Multiplexer #(.select(2)) multiplexer_2 (
    .in0(1'b0), .in1(1'b1), .in2(out_4), .in3(1'b1), .out(multiplexer_2_out), .sel(d_ff_1_q), .en(en));
  xnor xnor_1 (xnor_1_out, d_ff_1_q[0], d_ff_1_q[1]);
  D_Flip_Flop d_ff_1 (
    .clk(clock_1_out), .D(multiplexer_1_out), .Q(d_ff_1_q[0]), .Qn(d_ff_1_qn), .en(en), .reset(RST));  // open: preset
  D_Flip_Flop d_ff_2 (
    .clk(clock_1_out), .D(multiplexer_2_out), .Q(d_ff_1_q[1]), .Qn(d_ff_2_qn), .en(en), .reset(RST));  // open: preset
  Register A (.D(register_1_q), .Q(A_q), .clk(and_1_out), .clr(RST));  // open: en
  Register register_1 (.D(in_3), .Q(register_1_q), .clk(xnor_1_out), .clr(RST));  // open: en
  assign controlled_buffer_1_out = and_2_out ? A_q : 8'bz;  // Controlled_Buffer controlled_buffer_1
  assign controlled_buffer_2_out = and_2_out ? register_1_q : 8'bz;  // Controlled_Buffer controlled_buffer_2
  and and_2 (and_2_out, d_ff_1_q[1], d_ff_1_qn);
  Comparator comparator_1 (.a(controlled_buffer_1_out), .b(controlled_buffer_2_out), .gt(out_4));  // open: eq, lt

  // Notes on the sheet:
  //   T
  //   LDRA
  //   B
  //   LDRB
  //   CAP
  //   A>B
endmodule
