// Logisim project 累加器 定序型.circ as structural Verilog: 1 circuit, main circuit main
module main (
  input  en,
  input  RST,
  input  [7:0] in_3,
  output out_4
);

  wire A_q, A_qn, adder_1_cout, and_1_out, and_2_out, and_3_out, and_4_out, clock_1_out, d_ff_1_q, d_ff_1_qn,
       d_ff_2_q, d_ff_2_qn, not_1_out, or_1_out, or_2_out, or_3_out;
  wire [7:0] adder_1_out, controlled_buffer_1_out, register_1_q, register_2_q;

  Clock clock_1 (.out(clock_1_out));
  or or_1 (or_1_out, A_q, d_ff_2_q);
  not not_1 (not_1_out, clock_1_out);
  Register register_1 (.D(in_3), .en(en), .Q(register_1_q), .clk(and_1_out), .clr(RST));
  and and_1 (and_1_out, or_1_out, not_1_out);
  Register register_2 (.D(adder_1_out), .en(en), .Q(register_2_q), .clk(and_2_out), .clr(RST));
  and and_2 (and_2_out, d_ff_1_q, not_1_out);
  D_Flip_Flop A (.clk(clock_1_out), .D(and_3_out), .Q(A_q), .Qn(A_qn), .en(en), .reset(RST));  // open: preset
  D_Flip_Flop d_ff_1 (
    .clk(clock_1_out), .D(or_2_out), .Q(d_ff_1_q), .Qn(d_ff_1_qn), .en(en), .reset(RST));  // open: preset
  D_Flip_Flop d_ff_2 (
    .clk(clock_1_out), .D(d_ff_1_q), .Q(d_ff_2_q), .Qn(d_ff_2_qn), .en(en), .reset(RST));  // open: preset
  or or_2 (or_2_out, d_ff_2_q, A_q);
  and and_3 (and_3_out, d_ff_1_qn, A_qn, d_ff_2_qn);
  and and_4 (and_4_out, not_1_out, d_ff_1_q);
  or or_3 (or_3_out, d_ff_2_q, d_ff_1_q);
  assign controlled_buffer_1_out = or_3_out ? register_2_q : 8'bz;  // Controlled_Buffer controlled_buffer_1
  Adder adder_1 (.a(register_1_q), .b(controlled_buffer_1_out), .out(adder_1_out), .cout(adder_1_cout));  // open: cin
  Register #(.width(1)) register_3 (.D(adder_1_cout), .en(en), .Q(out_4), .clk(and_4_out), .clr(A_q));

  // Notes on the sheet:
  //   T
  //   LDA
  //   LDB
  //   B
  //   C
  //   LDC
  //   ADD
  //   ~CLR
endmodule
