// Logisim project 累加器 计数器.circ as structural Verilog: 1 circuit, main circuit main
module main (
  input  en,
  input  RST,
  input  [7:0] in_3,
  input  in_4,
  input  in_5,
  output out_6
);

  wire adder_1_cout, and_1_out, and_2_out, and_3_out, and_4_out, and_5_out, and_6_out, clock_1_out, d_ff_1_q,
       d_ff_1_qn, d_ff_2_q, d_ff_2_qn, nor_1_out, not_1_out, not_2_out, not_3_out, or_1_out, or_2_out,
       or_3_out, xor_1_out;
  wire [7:0] adder_1_out, controlled_buffer_1_out, register_1_q, register_2_q;

  and and_1 (and_1_out, d_ff_2_qn, d_ff_1_qn);
  not not_1 (not_1_out, in_4);
  not not_2 (not_2_out, in_5);
  Clock clock_1 (.out(clock_1_out));
  xor xor_1 (xor_1_out, d_ff_2_q, d_ff_1_q);
  or or_1 (or_1_out, and_1_out, and_2_out);
  and and_2 (and_2_out, d_ff_2_q, d_ff_1_q);
  or or_2 (or_2_out, in_4, in_5);
  or or_3 (or_3_out, not_1_out, not_2_out);
  not not_3 (not_3_out, clock_1_out);
  Register register_1 (.D(in_3), .en(en), .Q(register_1_q), .clk(and_3_out), .clr(RST));
  and and_3 (and_3_out, or_1_out, not_3_out);
  Register register_2 (.D(adder_1_out), .en(en), .Q(register_2_q), .clk(and_4_out), .clr(RST));
  and and_4 (and_4_out, xor_1_out, not_3_out);
  D_Flip_Flop d_ff_1 (
    .clk(clock_1_out), .D(or_2_out), .Q(d_ff_1_q), .Qn(d_ff_1_qn), .en(en), .reset(RST));  // open: preset
  D_Flip_Flop d_ff_2 (
    .clk(clock_1_out), .D(or_3_out), .Q(d_ff_2_q), .Qn(d_ff_2_qn), .en(en), .reset(RST));  // open: preset
  and and_5 (and_5_out, not_3_out, and_6_out);
  and and_6 (and_6_out, d_ff_2_q, d_ff_1_qn);
  assign controlled_buffer_1_out = and_6_out ? register_2_q : 8'bz;  // Controlled_Buffer controlled_buffer_1
  nor nor_1 (nor_1_out, d_ff_2_q, d_ff_1_q);
  Adder adder_1 (.a(register_1_q), .b(controlled_buffer_1_out), .out(adder_1_out), .cout(adder_1_cout));  // open: cin
  Register #(.width(1)) register_3 (.D(adder_1_cout), .en(en), .Q(out_6), .clk(and_5_out), .clr(nor_1_out));

  // Notes on the sheet:
  //   T
  //   LDA
  //   LDB
  //   ADD
  //   ~CLR
endmodule
