// Logisim project 累加器 选择器.circ as structural Verilog: 1 circuit, main circuit main
module main (
  input  en,
  input  RST,
  input  [7:0] in_3,
  output out_4
);

  wire adder_1_cout, and_1_out, and_2_out, and_3_out, and_4_out, and_5_out, clock_1_out, d_ff_1_qn,
       d_ff_2_qn, multiplexer_1_out, multiplexer_2_out, nor_1_out, not_1_out, or_1_out, xor_1_out;
  wire [1:0] d_ff_1_q;
  wire [7:0] adder_1_out, controlled_buffer_1_out, register_1_q, register_2_q;

  Clock clock_1 (.out(clock_1_out));
  or or_1 (or_1_out, and_1_out, and_2_out);
  and and_1 (and_1_out, d_ff_1_qn, d_ff_2_qn);
  xor xor_1 (xor_1_out, d_ff_1_q[0], d_ff_1_q[1]);
  and and_2 (and_2_out, d_ff_1_q[0], d_ff_1_q[1]);
  Multiplexer #(.select(2)) multiplexer_1 (
    .in0(1'b0), .in1(1'b1), .in2(1'b0), .in3(1'b0), .out(multiplexer_1_out), .sel(d_ff_1_q), .en(en));
  Multiplexer #(.select(2)) multiplexer_2 (
    .in0(1'b1), .in1(1'b1), .in2(1'b0), .in3(1'b1), .out(multiplexer_2_out), .sel(d_ff_1_q), .en(en));
  and and_3 (and_3_out, or_1_out, not_1_out);
  and and_4 (and_4_out, xor_1_out, not_1_out);
  not not_1 (not_1_out, clock_1_out);
  Register register_1 (.D(in_3), .en(en), .Q(register_1_q), .clk(and_3_out), .clr(RST));
  Register register_2 (.D(adder_1_out), .en(en), .Q(register_2_q), .clk(and_4_out), .clr(RST));
  D_Flip_Flop d_ff_1 (
    .clk(clock_1_out), .D(multiplexer_2_out), .Q(d_ff_1_q[0]), .Qn(d_ff_1_qn), .en(en), .reset(RST));  // open: preset
  D_Flip_Flop d_ff_2 (
    .clk(clock_1_out), .D(multiplexer_1_out), .Q(d_ff_1_q[1]), .Qn(d_ff_2_qn), .en(en), .reset(RST));  // open: preset
  and and_5 (and_5_out, not_1_out, d_ff_1_qn, d_ff_1_q[1]);
  assign controlled_buffer_1_out = d_ff_1_q[0] ? register_2_q : 8'bz;  // Controlled_Buffer controlled_buffer_1
  Adder adder_1 (.a(register_1_q), .b(controlled_buffer_1_out), .out(adder_1_out), .cout(adder_1_cout));  // open: cin
  nor nor_1 (nor_1_out, d_ff_1_qn, d_ff_2_qn);
  Register #(.width(1)) register_3 (.D(adder_1_cout), .en(en), .Q(out_4), .clk(and_5_out), .clr(nor_1_out));

  // Notes on the sheet:
  //   T
  //   LDA
  //   LDB
  //   ADD
  //   ~CLR
endmodule
